# Fritzing sketch AlarmClock (saved by Fritzing 0.9.3b)
breadboards: 1

parts:
  Part1 = Arduino Uno (Rev3)
  R1 = Resistor [tolerance=±5% resistance=220 package=THT]
  down = Pushbutton [package="[THT]"]
  mode = Pushbutton [package="[THT]"]
  R4 = Resistor [tolerance=±5% resistance=220 package=THT]
  R5 = Resistor [tolerance=±5% resistance=220 package=THT]
  piezo = Piezo Speaker
  sunrise = LED - 5mm [color="Orange (612nm)" package="5 mm [THT]"]
  info = LED - 5mm [color="Green (565nm)" package="5 mm [THT]"]
  lcd = LCD screen
  R6 = Rotary Potentiometer (Small) [maximum_resistance=100kΩ package=THT]
  up = Pushbutton [package="[THT]"]
  R7 = Resistor [tolerance=±5% resistance=220 package=THT]
  R8 = Resistor [tolerance=±5% resistance=220 package=THT]

nets:
  N1: Part1.D8, lcd.RS
  N2: Part1.D9_PWM, lcd.E
  N3: Part1.D10_PWM/SS, lcd.DB4
  N4: Part1.D11_PWM/MOSI, lcd.DB5
  N5: Part1.D12/MISO, lcd.DB6
  N6: Part1.D13/SCK, lcd.DB7
  GND: Part1.GND, R1.Pin_1, R4.Pin_1, R5.Pin_1, piezo.pin1, lcd.VSS, lcd.R/W, lcd.LED-, R6.leg2, R7.Pin_0, R8.Pin_0
  N7: Part1.D2, R1.Pin_0, up.Pin_1, up.Pin_2
  N8: Part1.D3_PWM, down.Pin_1, down.Pin_2, R4.Pin_0
  N9: Part1.D4, mode.Pin_1, mode.Pin_2, R5.Pin_0
  N10: Part1.D5_PWM, info.anode
  N11: Part1.D6_PWM, sunrise.anode
  N12: Part1.D7, piezo.pin2
  5V: Part1.5V, down.Pin_3, down.Pin_4, mode.Pin_3, mode.Pin_4, lcd.VDD, lcd.LED+, R6.leg1, up.Pin_3, up.Pin_4
  N13: sunrise.cathode, R8.Pin_1
  N14: info.cathode, R7.Pin_1
  N15: lcd.V0, R6.wiper
